# Fritzing sketch votbox (saved by Fritzing 0.9.2b)

parts:
  Matrix_keypad1 = KEYPAD 4x4  # not connected
  LED1 = smd LED [color="Red (633nm)" package="0805 [SMD]"]
  LED2 = smd LED [color="Green (560nm)" package="0805 [SMD]"]
  R1 = Resistor [tolerance=±5% resistance=220 package=THT]
  R2 = Resistor [tolerance=±5% resistance=220 package=THT]
  J1 = male pin header, 2 pins [form="♂ (male)"]
  J2 = male pin header, 3 pins [form="♂ (male)"]
  J3 = male pin header, 2 pins [form="♂ (male)"]
  D1 = Rectifier Diode [part_number=1N4001 package="300 mil [THT]"]
  R3 = Resistor [tolerance=±5% resistance=220 package=THT]  # not connected
  U1 = ESP8266 ESP12E WiFi Module [part_number=ESP8266]

nets:
  N1: LED1.cathode, R1.Pin_0
  N2: LED2.cathode, R2.Pin_1
  N3: R1.Pin_1, R2.Pin_0, J1.pin1, J2.pin2, J3.pin1
  N4: J1.pin2, D1.anode
  N5: J2.pin1, U1.TXD
  N6: J2.pin3, U1.RXD
  N7: J3.pin2, U1.GPIO_0

custom parts:
  KEYPAD 4x4: Matrix keypad 16 buttons, 4 rows x 4 columns
  ESP8266 ESP12E WiFi Module: Generic WiFi Module based on the ESP8266 with onboard PCB antenna and UART communications
